// Logisim project 7digit.circ as structural Verilog: 1 circuit, main circuit 7digit
module _7digit (
  input  x_3,
  input  x_2,
  input  x_1,
  input  x_0,
  output a,
  output b,
  output c,
  output d,
  output e,
  output f,
  output g
);

  wire and_2_out, and_3_out, and_4_out, and_5_out, and_6_out, and_7_out, and_10_out, and_11_out, and_12_out,
       not_1_out, not_2_out, not_3_out, not_4_out, not_5_out, not_6_out, not_7_out, not_8_out, not_9_out,
       not_10_out, not_11_out, not_12_out, not_13_out, not_14_out, not_15_out, not_16_out, not_17_out,
       not_18_out, not_19_out, not_20_out, not_21_out, or_1_out, or_2_out, or_3_out, or_4_out, or_5_out,
       or_6_out;

  or or_1 (or_1_out, x_0, x_2);
  not not_1 (not_1_out, x_1);
  not not_2 (not_2_out, x_0);
  or or_2 (or_2_out, not_2_out, not_3_out);
  not not_3 (not_3_out, x_2);
  not not_4 (not_4_out, x_3);
  or or_3 (or_3_out, x_0, x_1);
  not not_5 (not_5_out, x_0);
  or or_4 (or_4_out, not_5_out, not_6_out);
  not not_6 (not_6_out, x_1);
  or or_5 (or_5_out, x_2, x_3);
  or or_6 (or_6_out, x_2, not_7_out);
  not not_7 (not_7_out, x_3);
  not not_8 (not_8_out, x_0);
  and and_1 (c, not_8_out, x_1, not_9_out);
  not not_9 (not_9_out, x_2);
  not not_10 (not_10_out, x_3);
  not not_11 (not_11_out, x_2);
  not not_12 (not_12_out, x_1);
  not not_13 (not_13_out, x_1);
  not not_14 (not_14_out, x_0);
  and and_2 (and_2_out, x_2, not_15_out);
  not not_15 (not_15_out, x_1);
  not not_16 (not_16_out, x_3);
  not not_17 (not_17_out, x_2);
  and and_3 (and_3_out, not_16_out, not_17_out, x_0);
  not not_18 (not_18_out, x_2);
  and and_4 (and_4_out, not_18_out, x_1);
  and and_5 (and_5_out, x_1, x_0);
  not not_19 (not_19_out, x_3);
  and and_6 (and_6_out, not_19_out, not_20_out, not_21_out);
  not not_20 (not_20_out, x_2);
  not not_21 (not_21_out, x_1);
  and and_7 (and_7_out, x_2, x_1, x_0);
  and and_8 (a, or_1_out, not_1_out, or_2_out, not_4_out);
  and and_9 (b, or_3_out, or_4_out, or_5_out, or_6_out);
  and and_10 (and_10_out, not_10_out, not_11_out, not_12_out, x_0);
  or or_7 (d, and_10_out, and_11_out, and_12_out);
  and and_11 (and_11_out, x_2, not_13_out, not_14_out);
  and and_12 (and_12_out, x_2, x_1, x_0);
  or or_8 (e, x_0, and_2_out);
  or or_9 (f, and_3_out, and_4_out, and_5_out);
  or or_10 (g, and_6_out, and_7_out);
endmodule
