// Logisim project main_POTEC_project.circ as structural Verilog: 1 circuit, main circuit main
module main (
  input  [3:0] in_1
);

  wire n7digit_1_a, n7digit_1_b, n7digit_1_c, n7digit_1_d, n7digit_1_e, n7digit_1_f, n7digit_1_g;

  _7digit u_7digit_1 (
    .x3(in_1[3]), .x2(in_1[2]), .x1(in_1[1]), .x0(in_1[0]), .a(n7digit_1_a), .b(n7digit_1_b),
    .c(n7digit_1_c), .d(n7digit_1_d), .e(n7digit_1_e), .f(n7digit_1_f), .g(n7digit_1_g));
  _7_Segment_Display u_7_segment_display_1 (
    .g(n7digit_1_g), .f(n7digit_1_f), .a(n7digit_1_a), .b(n7digit_1_b), .e(n7digit_1_e), .d(n7digit_1_d),
    .c(n7digit_1_c));  // open: dp
endmodule
